# Fritzing sketch sketch (saved by Fritzing 0.4.3b)
breadboards: 2

parts:
  Arduino1 = Arduino
  U1 = 74HC595 [package="DIP16 [THT]"]
  R1 = 330 Ω Resistor [package=THT]
  LED1 = Red LED - 5mm
  R1_2 = 330 Ω Resistor [package=THT]
  R1_3 = 330 Ω Resistor [package=THT]
  R1_4 = 330 Ω Resistor [package=THT]
  R1_5 = 330 Ω Resistor [package=THT]
  R1_6 = 330 Ω Resistor [package=THT]
  R1_7 = 330 Ω Resistor [package=THT]
  R1_8 = 330 Ω Resistor [package=THT]
  LED1_2 = Red LED - 5mm
  LED1_3 = Red LED - 5mm
  LED1_4 = Red LED - 5mm
  LED1_5 = Red LED - 5mm
  LED1_6 = Red LED - 5mm
  LED1_7 = Red LED - 5mm
  LED1_8 = Red LED - 5mm

nets:
  GND: Arduino1.GND, U1.GND, U1.OE, LED1.cathode, LED1_2.cathode, LED1_3.cathode, LED1_4.cathode, LED1_5.cathode, LED1_6.cathode, LED1_7.cathode, LED1_8.cathode
  N1: Arduino1.D4, U1.ST_CP
  N2: Arduino1.D3, U1.SH_CP
  N3: Arduino1.D2, U1.DS
  +5V: Arduino1.+5V, U1.MR, U1.VCC
  N4: U1.Q1, R1_2.Pin_1
  N5: U1.Q2, R1_3.Pin_1
  N6: U1.Q3, R1_4.Pin_1
  N7: U1.Q4, R1_5.Pin_1
  N8: U1.Q5, R1_6.Pin_1
  N9: U1.Q6, R1_7.Pin_1
  N10: U1.Q7, R1_8.Pin_1
  N11: U1.Q0, R1.Pin_1
  N12: R1.Pin_0, LED1.anode
  N13: R1_2.Pin_0, LED1_2.anode
  N14: R1_3.Pin_0, LED1_3.anode
  N15: R1_4.Pin_0, LED1_4.anode
  N16: R1_5.Pin_0, LED1_5.anode
  N17: R1_6.Pin_0, LED1_6.anode
  N18: R1_7.Pin_0, LED1_7.anode
  N19: R1_8.Pin_0, LED1_8.anode
