# Fritzing sketch auto-beat-detection (saved by Fritzing 0.6.3b)
breadboards: 1

parts:
  Arduino1 = Arduino
  R2 = Resistor [tolerance=±5% resistance=220 package=THT]
  Beat_Indicator = LED - 5mm [color="Yellow (595nm)" package="5 mm [THT]"]
  C2 = Ceramic Capacitor [capacitance=4.7µF package="0805 [SMD, multilayer]"]
  R6 = Resistor [tolerance=±5% resistance=10k package=THT]
  R7 = Resistor [tolerance=±5% resistance=10k package=THT]
  C3 = Ceramic Capacitor [capacitance=0.1µF package="0805 [SMD, multilayer]"]
  R8 = Resistor [tolerance=±5% resistance=1k package=THT]
  R9 = Resistor [tolerance=±5% resistance=10k package=THT]
  MIC1 = Microphone
  U1 = LM 358 Dual Op-Amp [package="DIP8 [THT]"]
  R5 = Trimmer Potentiometer [maximum_resistance=100kΩ package=THT]

nets:
  N1: Arduino1.D11, Beat_Indicator.anode
  N2: Arduino1.+5V, R6.Pin_0, R9.Pin_0, U1.connector7
  N3: Arduino1.GND, R2.Pin_0, R7.Pin_1, MIC1.pin2, U1.connector3
  N4: Arduino1.A3, C2.0
  N5: R2.Pin_1, Beat_Indicator.cathode
  N6: C2.1, U1.connector0, R5.leg1, R5.wiper
  N7: R6.Pin_1, R7.Pin_0, U1.connector2
  N8: C3.0, R8.Pin_1
  N9: C3.1, R9.Pin_1, MIC1.pin1
  N10: R8.Pin_0, U1.connector1, R5.leg2
