# Fritzing sketch beatdetector (saved by Fritzing 0.4.3b)
breadboards: 1

parts:
  Arduino1 = Arduino
  LED1 = Red LED - 5mm
  R1 = 330 Ω Resistor [package=THT]
  R2 = 330 Ω Resistor [package=THT]
  Listen_Switch = Pushbutton [package="[THT]"]
  LED2 = green LED - 5mm
  Listen_Switch_2 = Pushbutton [package="[THT]"]
  R3 = 10k Ω Resistor [package=THT]
  R3_2 = 10k Ω Resistor [package=THT]

nets:
  N1: Arduino1.GND, R1.Pin_1, R2.Pin_1, R3.Pin_1, R3_2.Pin_1
  N2: Arduino1.D5, Listen_Switch.Pin_3, Listen_Switch.Pin_4, R3.Pin_0
  N3: Arduino1.D4, LED2.anode
  N4: Arduino1.D3, LED1.anode
  N5: Arduino1.D2, Listen_Switch_2.Pin_3, Listen_Switch_2.Pin_4, R3_2.Pin_0
  N6: Arduino1.+5V, Listen_Switch.Pin_1, Listen_Switch.Pin_2, Listen_Switch_2.Pin_1, Listen_Switch_2.Pin_2
  N7: LED1.cathode, R2.Pin_0
  N8: R1.Pin_0, LED2.cathode
