# Fritzing sketch dc-motor-control (saved by Fritzing 0.6.3b)
breadboards: 1

parts:
  IC1 = L293D [package=THT]
  VCC1 = Battery block 9V
  Arduino1 = Arduino
  M1 = DC Motor
  M2 = DC Motor
  C1 = Electrolytic Capacitor [capacitance=10µF package="100 mil [THT, electrolytic]"]

nets:
  N1: IC1.Enable_1, IC1.+V, Arduino1.+5V
  N2: IC1.In_1, Arduino1.D10
  N3: IC1.Out_1_(_Controlled_by_Enable_1_), M2.pin_1
  N4: IC1.0V, IC1.+Vmotor, VCC1.-, VCC1.+, C1.-, C1.+
  N5: IC1.Out_2_(_Controlled_by_Enable_1_), M2.pin_2
  N6: IC1.In_2, Arduino1.D9
  N7: IC1.Enable_2, Arduino1.GND
  N8: IC1.In_3, Arduino1.D5
  N9: IC1.Out_3_(_Controlled_by_Enable_2_), M1.pin_2
  N10: IC1.Out_4_(_Controlled_by_Enable_2_), M1.pin_1
  N11: IC1.In_4, Arduino1.D6
