# Fritzing sketch laser-projector-w-auto-beat-detection (saved by Fritzing 0.6.3b)
breadboards: 1

parts:
  IC1 = L293D [package=THT]
  VCC1 = Battery block 9V
  Arduino1 = Arduino
  M1 = DC Motor
  M2 = DC Motor
  Q1 = NPN-Transistor [package="TO92 [THT]"]
  Laser = LED - 5mm [color="Infrared (940nm)" package="5 mm [THT]"]
  R2 = Resistor [tolerance=±5% resistance=220 package=THT]
  Beat_Indicator = LED - 5mm [color="Yellow (595nm)" package="5 mm [THT]"]
  C1 = Electrolytic Capacitor [capacitance=10µF package="100 mil [THT, electrolytic]"]
  C2 = Ceramic Capacitor [capacitance=4.7µF package="0805 [SMD, multilayer]"]
  R6 = Resistor [tolerance=±5% resistance=10k package=THT]
  R7 = Resistor [tolerance=±5% resistance=10k package=THT]
  C3 = Ceramic Capacitor [capacitance=0.1µF package="0805 [SMD, multilayer]"]
  R8 = Resistor [tolerance=±5% resistance=1k package=THT]
  R9 = Resistor [tolerance=±5% resistance=10k package=THT]
  MIC1 = Microphone
  U1 = LM 358 Dual Op-Amp [package="DIP8 [THT]"]
  R5 = Trimmer Potentiometer [maximum_resistance=100kΩ package=THT]

nets:
  N1: IC1.Enable_1, IC1.+V, Arduino1.+5V, R6.Pin_0, R9.Pin_0, U1.connector7
  N2: IC1.In_1, Arduino1.D10
  N3: IC1.Out_1_(_Controlled_by_Enable_1_), M2.pin_1
  N4: IC1.0V, VCC1.-, C1.-
  N5: IC1.Out_2_(_Controlled_by_Enable_1_), M2.pin_2
  N6: IC1.In_2, Arduino1.D9
  N7: IC1.+Vmotor, VCC1.+, C1.+
  N8: IC1.Enable_2, Arduino1.GND, Laser.cathode, R2.Pin_0, R7.Pin_1, MIC1.pin2, U1.connector3
  N9: IC1.In_3, Arduino1.D5
  N10: IC1.Out_3_(_Controlled_by_Enable_2_), M1.pin_2
  N11: IC1.Out_4_(_Controlled_by_Enable_2_), M1.pin_1
  N12: IC1.In_4, Arduino1.D6
  N13: Arduino1.D12, Q1.B
  N14: Arduino1.D11, Beat_Indicator.anode
  N15: Arduino1.3V3, Q1.C
  N16: Arduino1.A3, C2.0
  N17: Q1.E, Laser.anode
  N18: R2.Pin_1, Beat_Indicator.cathode
  N19: C2.1, U1.connector0, R5.leg1, R5.wiper
  N20: R6.Pin_1, R7.Pin_0, U1.connector2
  N21: C3.0, R8.Pin_1
  N22: C3.1, R9.Pin_1, MIC1.pin1
  N23: R8.Pin_0, U1.connector1, R5.leg2
