# Fritzing sketch laser-projector-w-beat-detection (saved by Fritzing 0.6.3b)
breadboards: 1

parts:
  IC1 = L293D [package=THT]
  VCC1 = Battery block 9V
  Arduino1 = Arduino
  M1 = DC Motor
  M2 = DC Motor
  Q1 = NPN-Transistor [package="TO92 [THT]"]
  Laser = LED - 5mm [color="Infrared (940nm)" package="5 mm [THT]"]
  R1 = Resistor [tolerance=±5% resistance=10k package=THT]
  Reset = Pushbutton [package="[THT]"]
  R2 = Resistor [tolerance=±5% resistance=220 package=THT]
  Beat_Indicator = LED - 5mm [color="Yellow (595nm)" package="5 mm [THT]"]
  Learning_Indicator = LED - 5mm [color="Blue (525nm)" package="5 mm [THT]"]
  R3 = Resistor [tolerance=±5% resistance=220 package=THT]
  R4 = Resistor [tolerance=±5% resistance=10k package=THT]
  Beat_Tap = Pushbutton [package="[THT]"]
  C1 = Electrolytic Capacitor [capacitance=10µF package="100 mil [THT, electrolytic]"]

nets:
  N1: IC1.Enable_1, IC1.+V, Arduino1.+5V, Reset.Pin_3, Reset.Pin_4, Beat_Tap.Pin_3, Beat_Tap.Pin_4
  N2: IC1.In_1, Arduino1.D10
  N3: IC1.Out_1_(_Controlled_by_Enable_1_), M2.pin_1
  N4: IC1.0V, VCC1.-, C1.-
  N5: IC1.Out_2_(_Controlled_by_Enable_1_), M2.pin_2
  N6: IC1.In_2, Arduino1.D9
  N7: IC1.+Vmotor, VCC1.+, C1.+
  N8: IC1.Enable_2, Arduino1.GND, Laser.cathode, R1.Pin_0, R2.Pin_0, R3.Pin_0, R4.Pin_0
  N9: IC1.In_3, Arduino1.D5
  N10: IC1.Out_3_(_Controlled_by_Enable_2_), M1.pin_2
  N11: IC1.Out_4_(_Controlled_by_Enable_2_), M1.pin_1
  N12: IC1.In_4, Arduino1.D6
  N13: Arduino1.D13, Q1.B
  N14: Arduino1.D12, Learning_Indicator.anode
  N15: Arduino1.D11, Beat_Indicator.anode
  N16: Arduino1.D3, Reset.Pin_1, Reset.Pin_2, R4.Pin_1
  N17: Arduino1.D2, R1.Pin_1, Beat_Tap.Pin_1, Beat_Tap.Pin_2
  N18: Arduino1.3V3, Q1.C
  N19: Q1.E, Laser.anode
  N20: R2.Pin_1, Beat_Indicator.cathode
  N21: Learning_Indicator.cathode, R3.Pin_1
