# Fritzing sketch led-matrix (saved by Fritzing 0.4.3b)
breadboards: 1

parts:
  LED1 = Red LED - 5mm
  LED2 = Red LED - 5mm
  LED3 = Red LED - 5mm
  LED4 = Red LED - 5mm
  LED5 = Red LED - 5mm
  LED6 = Red LED - 5mm
  LED7 = Red LED - 5mm
  LED8 = Red LED - 5mm
  Voltage = female pin header, 8 pins [form="♀ (female)"]
  Ground = female pin header, 8 pins [form="♀ (female)"]
  LED1_2 = Red LED - 5mm
  LED2_2 = Red LED - 5mm
  LED3_2 = Red LED - 5mm
  LED4_2 = Red LED - 5mm
  LED5_2 = Red LED - 5mm
  LED6_2 = Red LED - 5mm
  LED7_2 = Red LED - 5mm
  LED8_2 = Red LED - 5mm
  LED1_3 = Red LED - 5mm
  LED2_3 = Red LED - 5mm
  LED3_3 = Red LED - 5mm
  LED4_3 = Red LED - 5mm
  LED5_3 = Red LED - 5mm
  LED6_3 = Red LED - 5mm
  LED7_3 = Red LED - 5mm
  LED8_3 = Red LED - 5mm
  LED1_4 = Red LED - 5mm
  LED2_4 = Red LED - 5mm
  LED3_4 = Red LED - 5mm
  LED4_4 = Red LED - 5mm
  LED5_4 = Red LED - 5mm
  LED6_4 = Red LED - 5mm
  LED7_4 = Red LED - 5mm
  LED8_4 = Red LED - 5mm
  LED1_5 = Red LED - 5mm
  LED2_5 = Red LED - 5mm
  LED3_5 = Red LED - 5mm
  LED4_5 = Red LED - 5mm
  LED5_5 = Red LED - 5mm
  LED6_5 = Red LED - 5mm
  LED7_5 = Red LED - 5mm
  LED8_5 = Red LED - 5mm
  LED1_6 = Red LED - 5mm
  LED2_6 = Red LED - 5mm
  LED3_6 = Red LED - 5mm
  LED4_6 = Red LED - 5mm
  LED5_6 = Red LED - 5mm
  LED6_6 = Red LED - 5mm
  LED7_6 = Red LED - 5mm
  LED8_6 = Red LED - 5mm
  LED1_7 = Red LED - 5mm
  LED2_7 = Red LED - 5mm
  LED3_7 = Red LED - 5mm
  LED4_7 = Red LED - 5mm
  LED5_7 = Red LED - 5mm
  LED6_7 = Red LED - 5mm
  LED7_7 = Red LED - 5mm
  LED8_7 = Red LED - 5mm
  LED1_8 = Red LED - 5mm
  LED2_8 = Red LED - 5mm
  LED3_8 = Red LED - 5mm
  LED4_8 = Red LED - 5mm
  LED5_8 = Red LED - 5mm
  LED6_8 = Red LED - 5mm
  LED7_8 = Red LED - 5mm
  LED8_8 = Red LED - 5mm

nets:
  N1: LED1.cathode, Ground.pin8, LED1_2.cathode, LED1_3.cathode, LED1_4.cathode, LED1_5.cathode, LED1_6.cathode, LED1_7.cathode, LED1_8.cathode
  N2: LED1.anode, LED2.anode, LED3.anode, LED4.anode, LED5.anode, LED6.anode, LED7.anode, LED8.anode, Voltage.pin1
  N3: Voltage.pin2, LED1_2.anode, LED2_2.anode, LED3_2.anode, LED4_2.anode, LED5_2.anode, LED6_2.anode, LED7_2.anode, LED8_2.anode
  N4: Voltage.pin3, LED1_3.anode, LED2_3.anode, LED3_3.anode, LED4_3.anode, LED5_3.anode, LED6_3.anode, LED7_3.anode, LED8_3.anode
  N5: Voltage.pin4, LED1_4.anode, LED2_4.anode, LED3_4.anode, LED4_4.anode, LED5_4.anode, LED6_4.anode, LED7_4.anode, LED8_4.anode
  N6: Voltage.pin5, LED1_5.anode, LED2_5.anode, LED3_5.anode, LED4_5.anode, LED5_5.anode, LED6_5.anode, LED7_5.anode, LED8_5.anode
  N7: Voltage.pin6, LED1_6.anode, LED2_6.anode, LED3_6.anode, LED4_6.anode, LED5_6.anode, LED6_6.anode, LED7_6.anode, LED8_6.anode
  N8: Voltage.pin7, LED1_7.anode, LED2_7.anode, LED3_7.anode, LED4_7.anode, LED5_7.anode, LED6_7.anode, LED7_7.anode, LED8_7.anode
  N9: Voltage.pin8, LED1_8.anode, LED2_8.anode, LED3_8.anode, LED4_8.anode, LED5_8.anode, LED6_8.anode, LED7_8.anode, LED8_8.anode
  N10: Ground.pin1, LED8_8.cathode
  N11: Ground.pin2, LED7_8.cathode
  N12: Ground.pin3, LED6_8.cathode
  N13: Ground.pin4, LED5_8.cathode
  N14: Ground.pin5, LED4_8.cathode
  N15: Ground.pin6, LED3_8.cathode
  N16: Ground.pin7, LED2_8.cathode
