# Fritzing sketch board (saved by Fritzing 0.7.11b)
breadboards: 2

parts:
  LPD8806_RGB_LED_Strip1 = LPD8806 RGB LED Strip
  Arduino1 = Arduino
  Power_plug1 = Power plug
  LPD8806_RGB_LED_Strip2 = LPD8806 RGB LED Strip
  R1 = Photocell (LDR) [package=THT]
  R2 = 1k Ω Resistor [package=THT]
  IR1 = TSOP312.., 314.. [package=THT]
  Pi2 = Adafruit Pi Cobbler
  IR2 = TSOP312.., 314.. [package=THT]
  LPD8806_RGB_LED_Strip3 = LPD8806 RGB LED Strip
  LPD8806_RGB_LED_Strip4 = LPD8806 RGB LED Strip
  Power_plug2 = Power plug

nets:
  GND: LPD8806_RGB_LED_Strip1.GND#0, Arduino1.GND, R2.Pin_1, IR1.GND
  N1: LPD8806_RGB_LED_Strip1.DI, Arduino1.D12
  N2: LPD8806_RGB_LED_Strip1.CI, Arduino1.D11
  GND_2: LPD8806_RGB_LED_Strip1.GND#4, Power_plug1.GND, LPD8806_RGB_LED_Strip2.GND
  N3: LPD8806_RGB_LED_Strip1.DO, LPD8806_RGB_LED_Strip2.DI
  N4: LPD8806_RGB_LED_Strip1.CO, LPD8806_RGB_LED_Strip2.CI
  +5V: LPD8806_RGB_LED_Strip1.+5V, Power_plug1.VCC, LPD8806_RGB_LED_Strip2.+5V
  N5: Arduino1.D2, IR1.Data
  N6: Arduino1.+5V, R1.pin_1, IR1.Vs
  N7: Arduino1.A0, R1.pin_0, R2.Pin_0
  N8: Pi2.3V3, IR2.Vs
  N9: Pi2.5V0, LPD8806_RGB_LED_Strip4.+5V#3
  GND_3: Pi2.GND, IR2.GND, LPD8806_RGB_LED_Strip4.GND#0
  N10: Pi2.PIN19, IR2.Data
  N11: Pi2.MOSI, LPD8806_RGB_LED_Strip4.DI
  N12: Pi2.SCLK, LPD8806_RGB_LED_Strip4.CI
  GND_4: LPD8806_RGB_LED_Strip3.GND, LPD8806_RGB_LED_Strip4.GND#4, Power_plug2.GND
  N13: LPD8806_RGB_LED_Strip3.DI, LPD8806_RGB_LED_Strip4.DO
  N14: LPD8806_RGB_LED_Strip3.CI, LPD8806_RGB_LED_Strip4.CO
  +5V_2: LPD8806_RGB_LED_Strip3.+5V, LPD8806_RGB_LED_Strip4.+5V#7, Power_plug2.VCC

notes:
  Couldn't find the right Fritzing part for the RGB LEDs used. It's not these strips, but instead: https://www.adafruit.com/products/738
  IR sensor tutorial here:
  http://learn.adafruit.com/ir-sensor/using-an-ir-sensor
  Photoresistor Tutorial Here:
  http://learn.adafruit.com/photocells/using-a-photocell

custom parts:
  LPD8806 RGB LED Strip: Digitally addressable RGB LED strip
  Adafruit Pi Cobbler: Adafruit Pi Cobbler GPIO Breakout for Raspberry Pi
