# Fritzing sketch LiveLights Core (saved by Fritzing 0.7.12b)
breadboards: 1

parts:
  Arduino1 = Arduino
  xbee1 = Adafruit Xbee Adapter [part_number=126]
  LPD8806_RGB_LED_Strip1 = LPD8806 RGB LED Strip
  LPD8806_RGB_LED_Strip2 = LPD8806 RGB LED Strip
  Power_plug2 = Power plug

nets:
  GND: Arduino1.GND, xbee1.GND, LPD8806_RGB_LED_Strip1.GND#0
  N1: Arduino1.D13, LPD8806_RGB_LED_Strip1.DI
  N2: Arduino1.D11, LPD8806_RGB_LED_Strip1.CI
  N3: Arduino1.D3, xbee1.TX
  N4: Arduino1.D2, xbee1.RX
  N5: Arduino1.3V3, xbee1.3V#0
  GND_2: LPD8806_RGB_LED_Strip1.GND#4, LPD8806_RGB_LED_Strip2.GND, Power_plug2.GND
  N6: LPD8806_RGB_LED_Strip1.DO, LPD8806_RGB_LED_Strip2.DI
  N7: LPD8806_RGB_LED_Strip1.CO, LPD8806_RGB_LED_Strip2.CI
  +5V: LPD8806_RGB_LED_Strip1.+5V, LPD8806_RGB_LED_Strip2.+5V, Power_plug2.VCC

custom parts:
  Adafruit Xbee Adapter: Xbee Adapter from Adadruit. Just the pin headers
  LPD8806 RGB LED Strip: Digitally addressable RGB LED strip
