# Fritzing sketch LiveLights Remote (saved by Fritzing 0.7.12b)
breadboards: 1

parts:
  Power_RGB3 = Prolight RGB 3 Watt Star
  Arduino1 = Arduino
  IC1 = ULN2803A [package=THT]
  R1 = 220 Ω Resistor [package=THT]
  Power_plug1 = Power plug
  R2 = 220 Ω Resistor [package=THT]
  R3 = 220 Ω Resistor [package=THT]
  xbee1 = Adafruit Xbee Adapter [part_number=126]

nets:
  N1: Power_RGB3.B+, R3.Pin_0
  N2: Power_RGB3.G+, R2.Pin_0
  N3: Power_RGB3.R+, R1.Pin_0
  GND: Power_RGB3.R-, Power_RGB3.G-, Power_RGB3.B-, Arduino1.GND, IC1.0V, Power_plug1.GND, xbee1.GND
  N4: Arduino1.D11, IC1.In_1
  N5: Arduino1.D10, IC1.In_2
  N6: Arduino1.D9, IC1.In_3
  N7: Arduino1.D3, xbee1.TX
  N8: Arduino1.D2, xbee1.RX
  N9: Arduino1.3V3, xbee1.3V#0
  VIN: Arduino1.VIN, IC1.COM_-_Common, Power_plug1.VCC
  N10: IC1.Out_3, R3.Pin_1
  N11: IC1.Out_2, R2.Pin_1
  N12: IC1.Out_1, R1.Pin_1

custom parts:
  Adafruit Xbee Adapter: Xbee Adapter from Adadruit. Just the pin headers
