# Fritzing sketch rhythm-keeper-with-chaser (saved by Fritzing 0.4.3b)
breadboards: 2

parts:
  SL = Red LED - 5mm
  330 = 330 Ω Resistor [package=THT]
  LS = Pushbutton [package="[THT]"]
  BL = green LED - 5mm
  LED3 = Blue LED - 5mm
  330_2 = 330 Ω Resistor [package=THT]
  LED3_2 = Blue LED - 5mm
  LED3_3 = Blue LED - 5mm
  LED3_4 = Blue LED - 5mm
  LED3_5 = Blue LED - 5mm
  LED3_6 = Blue LED - 5mm
  LED3_7 = Blue LED - 5mm
  LED3_8 = Blue LED - 5mm
  330_3 = 330 Ω Resistor [package=THT]
  330_4 = 330 Ω Resistor [package=THT]
  330_5 = 330 Ω Resistor [package=THT]
  330_6 = 330 Ω Resistor [package=THT]
  330_7 = 330 Ω Resistor [package=THT]
  330_8 = 330 Ω Resistor [package=THT]
  330_9 = 330 Ω Resistor [package=THT]
  330_10 = 330 Ω Resistor [package=THT]
  U1 = 74HC595 [package="DIP16 [THT]"]
  10k = 10k Ω Resistor [package=THT]
  Arduino1 = Arduino

nets:
  N1: SL.cathode, 330_10.Pin_0
  N2: SL.anode, Arduino1.D8
  GND: 330.Pin_0, 330_2.Pin_0, 330_3.Pin_0, 330_4.Pin_0, 330_5.Pin_0, 330_6.Pin_0, 330_7.Pin_0, 330_8.Pin_0, 330_9.Pin_0, 330_10.Pin_1, U1.GND, U1.OE, 10k.Pin_0, Arduino1.GND
  N3: 330.Pin_1, BL.cathode
  VCC: LS.Pin_1, LS.Pin_2, U1.MR, U1.VCC, Arduino1.+5V
  N4: LS.Pin_3, LS.Pin_4, 10k.Pin_1, Arduino1.D10
  N5: BL.anode, Arduino1.D9
  N6: LED3.cathode, 330_2.Pin_1
  N7: LED3.anode, U1.Q7
  N8: LED3_2.cathode, 330_3.Pin_1
  N9: LED3_2.anode, U1.Q6
  N10: LED3_3.cathode, 330_4.Pin_1
  N11: LED3_3.anode, U1.Q5
  N12: LED3_4.cathode, 330_5.Pin_1
  N13: LED3_4.anode, U1.Q4
  N14: LED3_5.cathode, 330_6.Pin_1
  N15: LED3_5.anode, U1.Q3
  N16: LED3_6.cathode, 330_7.Pin_1
  N17: LED3_6.anode, U1.Q2
  N18: LED3_7.cathode, 330_9.Pin_1
  N19: LED3_7.anode, U1.Q0
  N20: LED3_8.cathode, 330_8.Pin_1
  N21: LED3_8.anode, U1.Q1
  N22: U1.SH_CP, Arduino1.D4
  N23: U1.ST_CP, Arduino1.D3
  N24: U1.DS, Arduino1.D2
