# Fritzing sketch rhythm-keeper (saved by Fritzing 0.4.3b)
breadboards: 1

parts:
  SL = Red LED - 5mm
  330 = 330 Ω Resistor [package=THT]
  LS = Pushbutton [package="[THT]"]
  BL = green LED - 5mm
  330_2 = 330 Ω Resistor [package=THT]
  10k = 10k Ω Resistor [package=THT]
  Arduino1 = Arduino

nets:
  N1: SL.cathode, 330_2.Pin_0
  N2: SL.anode, Arduino1.D8
  N3: 330.Pin_0, 330_2.Pin_1, 10k.Pin_0, Arduino1.GND
  N4: 330.Pin_1, BL.cathode
  N5: LS.Pin_1, LS.Pin_2, Arduino1.+5V
  N6: LS.Pin_3, LS.Pin_4, 10k.Pin_1, Arduino1.D10
  N7: BL.anode, Arduino1.D9
