# Fritzing sketch board (saved by Fritzing 0.7.11b)
breadboards: 1

parts:
  Arduino1 = Arduino
  LED1 = LED - 3mm [color="Red (633nm)" package="3 mm [THT]"]
  LED2 = LED - 3mm [color="Red (633nm)" package="3 mm [THT]"]
  S1 = Pushbutton [package="[SMD]"]
  S2 = Pushbutton [package="[SMD]"]
  R3 = Resistor [tolerance=±5% resistance=10k package="0805 [SMD]"]
  R4 = Resistor [tolerance=±5% resistance=10k package="0805 [SMD]"]

nets:
  N1: Arduino1.D11, LED1.cathode
  N2: Arduino1.D10, LED2.cathode
  N3: Arduino1.D7, S1.Pin_1, S1.Pin_2, R3.Pin_0
  N4: Arduino1.D6, S2.Pin_1, S2.Pin_2, R4.Pin_0
  N5: Arduino1.+5V, S1.Pin_3, S1.Pin_4, S2.Pin_3, S2.Pin_4
  N6: Arduino1.GND, LED1.anode, LED2.anode, R3.Pin_1, R4.Pin_1
