# Fritzing sketch processing-control (saved by Fritzing 0.8.7b)
breadboards: 1

parts:
  xbee2 = artuino [part_number=126]
  Part1 = Arduino Uno (Rev3)
  LED1 = RGB LED (com. cathode, rbg) [package="5 mm [THT]"]

nets:
  N1: xbee2.3v#1, Part1.3V3
  N2: xbee2.rx, Part1.D3_PWM
  N3: xbee2.tx, Part1.D2
  N4: Part1.D9_PWM, LED1.green_anode
  N5: Part1.D10_PWM/SS, LED1.blue_anode
  N6: Part1.D11_PWM/MOSI, LED1.red_anode
  N7: Part1.5V, LED1.common_cathode

custom parts:
  artuino: Adafruit Xbee Adapter
